# Fritzing sketch 433_ds18b20 (saved by Fritzing 0.9.3b)
circuit board: 1.09357cm x 2.3355cm
breadboards: 1

parts:
  U2 = attiny85 [package=dip]
  R1 = Resistor [tolerance=±5% resistance=4.7k package="1206 [SMD]"]
  DS2 = DS18B20 1-Wire Temperature Sensor [part_number=DS18B20]
  U1 = FS1000A - 433Mhz RF Transmitter [package=THT]
  LED1 = smd LED [color="Red (633nm)" package="1206 [SMD]"]
  J1 = male pin header, 1 pin [form="♂ (male)"]
  J2 = male pin header, 1 pin [form="♂ (male)"]

nets:
  GND: U2.Pin_4, DS2.GND, U1.GND, LED1.cathode, J2.pin1
  N1: U2.Pin_5, LED1.anode
  N2: U2.Pin_6, R1.Pin_0, DS2.DQ
  N3: U2.Pin_7, U1.DATA
  VDD: U2.Pin_8, R1.Pin_1, DS2.VDD, U1.VCC, J1.pin1

notes:
  -
  +
  LED
  4.7k
  ATTINY85

custom parts:
  FS1000A - 433Mhz RF Transmitter: This is 433Mhz RF transmitter with receiver kit for Arduino ARM MCU wireless Application environment: Remote control switch, receiver module, motorcycles, automobile anti-theft products, home security products, electric doors, shutter doors, windows, remote control socket, remote control LED, remote audio remote control electric doors, garage door remote control, remote control retractable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
