# Fritzing sketch esp_ds18b20 (saved by Fritzing 0.9.2b)
circuit board: 1.91246cm x 1.74035cm
breadboards: 1

parts:
  LM1117 = Voltage Regulator [package=sot223]
  ESP-12 = ESP8266-12 WiFi Module [part_number=ESP8266]
  VCC = Header 1 [package=luxeon-pad]
  GND = Header 1 [package=luxeon-pad]
  4k7 = Resistor [tolerance=±5% resistance=4.7k package="1206 [SMD]"]
  3_3V = Header 1 [package=luxeon-pad]
  GND_2 = Header 1 [package=luxeon-pad]
  DATA1 = Header 1 [package=luxeon-pad]

nets:
  N1: LM1117.ADJ, ESP-12.GND, ESP-12.GPIO_15, GND.1, GND_2.1
  N2: LM1117.OUT, ESP-12.CH_PD, ESP-12.VCC, 4k7.Pin_0, 3_3V.1
  N3: LM1117.IN, VCC.1
  N4: ESP-12.GPIO_0, 4k7.Pin_1, DATA1.1

notes:
  VCC
  GND
  3.3
  ESP-8

custom parts:
  ESP8266-12 WiFi Module: Generic WiFi Module based on the ESP8266 with onboard PCB antenna and UART communications
