# Fritzing sketch esp8266_dht22_sketch (saved by Fritzing 0.9.3b)
breadboards: 1

parts:
  DHT = DHT22 Humidity and Temperature Sensor
  X2 = USB Connectors [package=usb-a-h]
  IC1 = Voltage Regulator [package=sot223]
  4k7 = Resistor [tolerance=±5% resistance=4.7k package=THT]
  ESP8266 = ESP8266 WiFi Module [part_number=ESP8266]

nets:
  VDD: DHT.VDD, IC1.OUT, 4k7.Pin_0, ESP8266.VCC, ESP8266.CH_PD
  N1: DHT.DATA, 4k7.Pin_1, ESP8266.GPIO_0
  GND: DHT.GND, X2.GND, IC1.ADJ, ESP8266.GND
  N2: X2.VBUS, IC1.IN

custom parts:
  ESP8266 WiFi Module: Generic WiFi Module based on the ESP8266 with onboard PCB antenna and UART communications
