# Fritzing sketch esp8266_ds18b20_sketch (saved by Fritzing 0.9.2b)
circuit board: 3.1823cm x 1.54087cm
breadboards: 1

parts:
  X2 = USB Connectors [package=usb-a-h]
  ESP8266 = ESP8266 WiFi Module [part_number=ESP8266]
  4k7 = Resistor [tolerance=±5% resistance=4.7k package=THT]
  IC1 = Voltage Regulator [package=sot223]
  J2 = screw terminal, 3 pins

nets:
  N1: X2.VBUS, IC1.IN
  GND: X2.GND, ESP8266.GND, IC1.ADJ, J2.pin1
  N2: ESP8266.VCC, ESP8266.CH_PD, 4k7.Pin_0, IC1.OUT, J2.pin3
  N3: ESP8266.GPIO_0, 4k7.Pin_1, J2.pin2

notes:
  GND
  5V
  3V
  RX
  TX
  DATA
  VDD
  GPIO0

custom parts:
  ESP8266 WiFi Module: Generic WiFi Module based on the ESP8266 with onboard PCB antenna and UART communications
