# Fritzing sketch ldr (saved by Fritzing 0.9.3b)
circuit board: 2.05367cm x 1.0706cm
breadboards: 1

parts:
  R2 = Resistor [tolerance=±5% resistance=50k package=THT]
  VCC1 = Battery
  VCC2 = Battery
  R3 = PHOTOCELL [package=photocell]
  Q1 = NPN-Transistor [package="TO92 [THT]"]
  LED2 = LED - 5mm [color="White (4500K)" package="5 mm [THT]"]

nets:
  N1: R2.Pin_0, R3.P$2, Q1.B
  N2: R2.Pin_1, VCC1.+, VCC2.+, LED2.anode
  N3: VCC1.-, VCC2.-, R3.P$1, Q1.E
  N4: Q1.C, LED2.cathode

notes:
  -
  +
  50k
  LDR
  NPN
  LED
