# Fritzing sketch optocoupler (saved by Fritzing 0.9.2b)
circuit board: 3.01978cm x 0.95753cm
breadboards: 1

parts:
  J1 = Screw terminal - 2 pins [package=THT]
  R1 = Resistor [tolerance=±5% resistance=200k package=THT]
  U1 = TLP621 [package=THT]
  J2 = female pin header, 3 pins [form="♀ (female)"]
  C2 = Electrolytic Capacitor [capacitance=100μF package="100 mil [THT, electrolytic]"]
  R2 = Resistor [tolerance=±5% resistance=390k package=THT]

nets:
  N1: J1.pin1, R1.Pin_1
  N2: J1.pin2, U1.Pin_1
  N3: R1.Pin_0, U1.Pin_2
  N4: U1.Pin_4, J2.pin1
  N5: U1.Pin_3, J2.pin2, C2.+, R2.Pin_1
  N6: J2.pin3, C2.-, R2.Pin_0

notes:
  L
  N
  K814P
  200k
  390k
  0.1uF
  3.3
  GND
  OUT
  bit.ly/2akQIc4
