# Fritzing sketch pizero_hat (saved by Fritzing 0.9.3b)
circuit board: 6.52541cm x 3.09829cm
breadboards: 1

parts:
  J1 = Raspberry Pi Zero
  Q1 = Crystal [frequency="25 MHz" package=THT]
  R2 = Resistor [tolerance=±5% resistance=10k package="1206 [SMD]"]
  R1 = Resistor [tolerance=±5% resistance=10k package="1206 [SMD]"]
  R5 = Resistor [tolerance=±5% resistance=1k package="1206 [SMD]"]
  R10 = Resistor [tolerance=±5% resistance=2.7k package="1206 [SMD]"]
  C1 = Capacitor [package=1206]
  C2 = Capacitor [package=1206]
  C3 = Capacitor Polarized [package=eia3216]
  C6 = Capacitor [package=1206]
  L1 = Inductors [package=inductor-1206]
  LED1 = LEDs [package=led-1206]
  U1 = ENC28J60 [package=ssop28db]
  J2 = HANRUN RJ-45 [package=hanrun]
  R4 = Resistor [tolerance=±5% resistance=1k package="1206 [SMD]"]
  R3 = Resistor [tolerance=±5% resistance=1k package="1206 [SMD]"]
  R7 = Resistor [tolerance=±1% resistance=49.9 package="1206 [SMD]"]
  R6 = Resistor [tolerance=±1% resistance=49.9 package="1206 [SMD]"]
  C4 = Capacitor [package=1206]
  C5 = Capacitor [package=1206]
  R8 = Resistor [tolerance=±1% resistance=49.9 package="1206 [SMD]"]
  R9 = Resistor [tolerance=±1% resistance=49.9 package="1206 [SMD]"]

nets:
  3V3: J1.3v3, J1.3V3, R2.Pin_0, R1.Pin_0, R5.Pin_0, L1.1, U1.VDDTX, U1.VDDRX, U1.VDDPLL, U1.VDDOSC, U1.VDD
  GND: J1.GND, R10.Pin_0, C1.2, C2.2, C3.-, C6.2, U1.VSS, U1.VSSRX, U1.VSSTX, U1.VSSPLL, U1.VSSOSC, J2.GND, J2.GLED-, J2.YLED-, J2.SHIELD, C4.2, C5.1
  N1: J1.GPIO10, U1.SI
  N2: J1.GPIO9, U1.SO
  N3: J1.GPIO11, U1.SCK
  N4: J1.GPIO8, R1.Pin_1, U1.CS
  N5: J1.GPIO25, U1._INT
  N6: Q1.pin_0, C2.1, U1.OSC1
  N7: Q1.pin_1, C1.1, U1.OSC2
  N8: R2.Pin_1, U1.RESET
  N9: R5.Pin_1, LED1.A
  N10: R10.Pin_1, U1.RBIAS
  N11: C3.+, U1.VCAP
  N12: C6.1, LED1.C
  N13: L1.2, J2.TDC
  N14: U1.TPIN-, J2.RD-, R9.Pin_0
  N15: U1.TPIN+, J2.RD+, R8.Pin_0
  N16: U1.TPOUT-, J2.TD-, R7.Pin_1
  N17: U1.TPOUT+, J2.TD+, R6.Pin_1
  N18: U1.LEDB, R4.Pin_0
  N19: U1.LEDA, R3.Pin_0
  N20: J2.RDC, C5.2, R8.Pin_1, R9.Pin_1
  N21: J2.GLED+, R3.Pin_1
  N22: J2.YLED+, R4.Pin_1
  N23: R7.Pin_0, R6.Pin_0, C4.1

custom parts:
  Raspberry Pi Zero: The Raspberry Pi Zero is half the size of a Model A+, with twice the utility. A tiny Raspberry Pi that’s affordable enough for any project! · 1Ghz, Single-core CPU · 512MB RAM · Mini HDMI and USB On-The-Go ports · Micro USB power · HAT-compatible 40-pin header. In this version schematic has been changed so the pins match the GPIO connector. I.e. the left hand pins are all the pins (the power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
  HANRUN RJ-45: RJ-45 with LEDs HANRUN HR911105A
